# Fritzing sketch fritzing (saved by Fritzing 0.9.3b)
circuit board: 8.46667cm x 5.64444cm
breadboards: 1

parts:
  Adafruit_HUZZAH_ESP8266_Breakout1 = Adafruit HUZZAH ESP8266 Breakout [part_number=2471]
  R1 = Resistor [tolerance=±5% resistance=22k package="1206 [SMD]"]
  S1 = Pushbutton [package="[SMD]"]
  R2 = Resistor [tolerance=±5% resistance=10k package="1206 [SMD]"]
  U1 = CAPSENSE_PAD [package=capsense_pad]

nets:
  N1: Adafruit_HUZZAH_ESP8266_Breakout1.GND, R2.Pin_1
  N2: Adafruit_HUZZAH_ESP8266_Breakout1.#12, R1.Pin_1, U1.RES
  N3: Adafruit_HUZZAH_ESP8266_Breakout1.#14, R1.Pin_0
  N4: Adafruit_HUZZAH_ESP8266_Breakout1.#16, S1.Pin_1, S1.Pin_2, R2.Pin_0
  N5: Adafruit_HUZZAH_ESP8266_Breakout1.3V, S1.Pin_3, S1.Pin_4

notes:
  20k resistor
